# Fritzing sketch Circuit diagram (saved by Fritzing 1.0.5)
# 18650 Li-ion Battery: CC-BY Dr Kristofer Chan, King's College London/Remote-research.org
breadboards: 2

parts:
  Motor_driver_1 = drv-1012
  Motor_driver_2 = drv-1012
  Motor_driver_3 = drv-1012
  Motor_2 = DC Motor [voltage_(max)=9V voltage_(min)=3V]
  Motor_3 = DC Motor [voltage_(max)=6V voltage_(min)=3V]
  Motor_1 = DC Motor [voltage_(max)=6V voltage_(min)=3V]
  Servo_1 = Basic Servo
  Servo_2 = Basic Servo
  Servo_3 = Basic Servo
  BAT2 = 18650 Li-ion Battery [package=battery-18650]
  BAT4 = 18650 Li-ion Battery [package=battery-18650]
  BAT1 = 18650 Li-ion Battery [package=battery-18650]
  Arduino_Due = Arduino Due (Rev2b)
  NRF24L01 = NRF24L01+ Breakout Board

nets (from the breadboard view):
  GND: Motor_driver_1.Pin_1, Motor_driver_2.Pin_1, Motor_driver_3.Pin_1, BAT4.-, Arduino_Due.GND, NRF24L01.GND
  N1: Motor_driver_1.Pin_2, Arduino_Due.A7
  N2: Motor_driver_1.Pin_3, Arduino_Due.D48
  N3: Motor_driver_1.Pin_4, Arduino_Due.D40
  5V: Motor_driver_1.Pin_5, Motor_driver_2.Pin_5, Motor_driver_3.Pin_5, Arduino_Due.5V, NRF24L01.VCC
  N4: Motor_driver_1.Pin_6, Arduino_Due.A6
  N5: Motor_driver_1.Pin_7, Arduino_Due.D49
  N6: Motor_driver_1.Pin_8, Arduino_Due.D41
  GND_2: Motor_driver_1.Pin_9, Motor_driver_2.Pin_9, Motor_driver_3.Pin_9, Servo_1.gnd, Servo_2.gnd, Servo_3.gnd, BAT2.-, BAT1.-
  VCC: Motor_driver_1.Pin_10, Motor_driver_2.Pin_10, Motor_driver_3.Pin_10, Servo_1.vcc, Servo_2.vcc, Servo_3.vcc, BAT2.+, BAT1.+
  N7: Motor_driver_1.Pin_11, Motor_1.pin_2
  N8: Motor_driver_1.Pin_12, Motor_1.pin_1
  N9: Motor_driver_2.Pin_2, Arduino_Due.A9
  N10: Motor_driver_2.Pin_3, Arduino_Due.D50
  N11: Motor_driver_2.Pin_4, Arduino_Due.D42
  N12: Motor_driver_2.Pin_6, Arduino_Due.A8
  N13: Motor_driver_2.Pin_7, Arduino_Due.D51
  N14: Motor_driver_2.Pin_8, Arduino_Due.D43
  N15: Motor_driver_2.Pin_11, Motor_2.pin_2
  N16: Motor_driver_2.Pin_12, Motor_2.pin_1
  N17: Motor_driver_3.Pin_2, Arduino_Due.A11
  N18: Motor_driver_3.Pin_3, Arduino_Due.D52
  N19: Motor_driver_3.Pin_4, Arduino_Due.D44
  N20: Motor_driver_3.Pin_6, Arduino_Due.A10
  N21: Motor_driver_3.Pin_7, Arduino_Due.D53
  N22: Motor_driver_3.Pin_8, Arduino_Due.D45
  N23: Motor_driver_3.Pin_11, Motor_3.pin_2
  N24: Motor_driver_3.Pin_12, Motor_3.pin_1
  N25: Servo_1.pulse, Arduino_Due.D4_PWM/SS1
  N26: Servo_2.pulse, Arduino_Due.D2_PWM
  N27: Servo_3.pulse, Arduino_Due.D3_PWM
  N28: BAT4.+, Arduino_Due.VIN
  N29: Arduino_Due.D23, NRF24L01.CE
  N30: Arduino_Due.D25, NRF24L01.CS

notes:
  SPI pins aren't connected because the Arduino Due model for fritzing didn't connect them in PCB editor and fritzing doesn't make it easy to modify built-in parts
  Servos have pulse from arduino, but power from motor power

custom parts:
  drv-1012: .The BTS7960 is a fully integrated high current H bridge module for motor drive applications.
  18650 Li-ion Battery: 18650 li-ion Battery Standard 18650 battery with interactive connectors Creative Common Attribution 4.0 International (CC-BY 4.0) license. Any use of this part requires attribution of Dr Kristofer Chan, Department of Geography, King's College London. Contact kristofer.chan [at] kcl.ac.uk OR kris [at] remote-research.org for further information.
