# Fritzing sketch Controller diagram (saved by Fritzing 1.0.5)

parts:
  Part1 = Arduino Mega 2560 (Rev3)
  Part2 = Thumb Joystick
  Part3 = Thumb Joystick
  Part4 = NRF24L01+ Breakout Board

nets:
  N1: Part1.A0, Part3.HORZ
  N2: Part1.A1, Part3.VERT
  N3: Part1.A2, Part2.HORZ
  N4: Part1.A3, Part2.VERT
  3.3V: Part1.3V3, Part4.VCC
  GND: Part1.GND, Part2.GND, Part3.GND, Part4.GND
  5V: Part1.5V, Part2.VCC, Part3.VCC
  N5: Part1.D48, Part4.CS
  N6: Part1.D49, Part4.CE
  N7: Part1.D50, Part4.MISO
  N8: Part1.D51, Part4.MOSI
  N9: Part1.D52, Part4.SCK

notes:
  SPI pins:
  SCK: 52,
  MO: 51
  MI: 50
  CE: 49
  CSN: 48
